// Logisim project flipflop.circ as structural Verilog: 1 circuit, main circuit asynkron Clear
module asynkron_Clear (
  input  D,
  input  Clear,
  output Q,
  output Q_prime
);

  wire Clock_out, nand_1_out, nand_2_out, nand_3_out, nand_4_out, nand_5_out, nand_6_out, not_1_out;

  Clock #(.highDuration(5), .lowDuration(5)) Clock (.out(Clock_out));
  nand nand_1 (nand_1_out, nand_4_out, nand_2_out);
  nand nand_2 (nand_2_out, nand_1_out, Clock_out);
  nand nand_3 (nand_3_out, nand_2_out, Clock_out, nand_4_out);
  nand nand_4 (nand_4_out, nand_3_out, D);
  nand nand_5 (nand_5_out, nand_2_out, nand_6_out);
  nand nand_6 (nand_6_out, nand_5_out, nand_3_out);
  and and_1 (Q, nand_5_out, not_1_out);
  not not_1 (not_1_out, Clear);
  or or_1 (Q_prime, nand_6_out, Clear);

  // Notes on the sheet:
  //   D  Flip Flop med asynkron CLEAR
endmodule
